# Fritzing sketch fritzing_drawing (saved by Fritzing 0.9.6b)

parts:
  DRV_1 = DRV 8825 Stepper Motor Carrier, High Current [part_number="DRV 8825"]
  U2 = POT [package=pot_alpha_rv16af-20]
  J3 = Power Jack [package=power_jack_smd]
  M3 = DOIT Esp32 DevKit v1 (30 pins long, 11 pins width) [part_number=ESP32S-PIN30]
  IC2 = Voltage Regulator [package=to-220-alt]
  C2 = Capacitor Polarized [package=panasonic_c]  # not connected
  C1 = Electrolytic Capacitor [capacitance=100µF voltage=35V package="200 mil [THT, electrolytic]"]
  C3 = Capacitor [package=cap-pth-small2]  # not connected
  M2 = Stepper Motor - Bipolar

nets:
  N1: DRV_1.ENABLE, M3.D14
  N2: DRV_1.MS1, M3.D27
  N3: DRV_1.MS2, M3.D26
  N4: DRV_1.MS3, M3.D25
  N5: DRV_1.STEP, M3.D35
  N6: DRV_1.DIRECTION, M3.D34
  N7: DRV_1.VOLTAGE_ST/_MT, J3.GND, C1.+
  N8: DRV_1.OUT_2B, M2.A
  N9: DRV_1.OUT_2A, M2.C
  N10: DRV_1.OUT_1A, M2.B
  N11: DRV_1.OUT_1B, M2.D
  N12: U2.A, M3.GND
  N13: U2.S, M3.D5
  N14: U2.E, M3.3V3
  N15: J3.GNDBREAK, C1.-
  N16: M3.VIN, IC2.OUT

notes:
  Don't forget to set Vref on trimer to limit motor current. Imax = Vref*2
  100u/35V
  10u/35V
  100n
  7805
  12V

custom parts:
  DOIT Esp32 DevKit v1 (30 pins long, 11 pins width): The DOIT Esp32 DevKit v1 is one of the development board created by DOIT to evaluate the ESP-WROOM-32 module. It is based on the ESP32 microcontroller that boasts Wifi, Bluetooth, Ethernet and Low Power support all in a single chip. (vanepp) made breadboard work, adjusted pin numbering and labels and reduced size of schematic and cleaned up pcb. This chip is 30pins long (2 x15) and 11 pins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
